// Logisim project offline1_v2.circ as structural Verilog: 1 circuit, main circuit main
module main (
  input  cs2,
  input  cs1,
  input  cs0,
  input  A3,
  input  A2,
  input  A1,
  input  A0,
  input  B3,
  input  B2,
  input  B1,
  input  B0,
  output Z,
  output C,
  output S,
  output V,
  output out_16,
  output out_17,
  output out_18,
  output out_19
);
endmodule
