// Logisim project main.circ as structural Verilog
module ControlUnit (
  input  [3:0] OPCODE
);

  wire [11:0] rom_1_data;

  ROM #(.addrWidth(4), .dataWidth(12)) rom_1 (.addr(OPCODE), .data(rom_1_data));  // open: sel

  // Notes on the sheet:
  //   contents of rom_1 (hex, n*v repeats v):
  //   adf
endmodule
